# Fritzing sketch Alchol Concentration (saved by Fritzing 0.9.3b)
breadboards: 1

parts:
  부품1 = MQ-3 breakout
  부품2 = Arduino Uno (Rev3)
  C2 = Capacitor [package=cap-pth-small2]
  L1 = Inductor [package="0805 [SMD]"]
  D1 = Zener Diode [part_number=1N5231-5.1V breakdown_voltage=5.1V package="Melf DO-213 AB [SMD]"]
  D2 = Schottky Diode [part_number=1N5817 package="300 mil [THT]"]
  부품3 = LCD1602-I2C
  S1 = Pushbutton [package="[SMD]"]
  C3 = Capacitor Polarized [package=cpol-radial-100uf-25v]
  R1 = Resistor [tolerance=±5% resistance=10k package=THT]

nets:
  5V: 부품1.VCC, 부품2.5V, C2.1, L1.pin_0, D1.cathode, D2.cathode, 부품3.VCC, C3.+, R1.Pin_1
  GND: 부품1.GND, 부품2.GND, C2.2, L1.pin_1, D1.anode, D2.anode, 부품3.GND, S1.Pin_3, S1.Pin_4, C3.-
  N1: 부품1.AO, 부품2.A0
  N2: 부품2.A4/SDA, 부품3.SDA
  N3: 부품2.D10_PWM/SS, S1.Pin_1, S1.Pin_2, R1.Pin_0
  N4: 부품2.A5/SCL, 부품3.SCL

custom parts:
  MQ-3 breakout: Alcohol sensor is capable of detecting alcohol (ethanol) particles on itself and gives the information in digital form back to us to manipulate with it. SKU:101251 • Voltage: 5V DC • Power: max 750mW • Measurement range: 0.04-4mg/L
  LCD1602-I2C: A standard character display, usually with 2x16 characters. Comes in many colors with LCM1602 IIC attached.
